// Logisim project risc_v_rv32im (both versions).circ as structural Verilog: 1 circuit, main circuit System_JAVA
module System_JAVA (
);

  wire and_1_out, and_3_out, and_4_out, and_5_out, and_6_out, and_7_out, and_8_out, and_9_out, and_10_out,
       and_11_out, and_12_out, and_13_out, and_14_out, button_3_out, button_4_out, clock_1_out, clock_2_out,
       clock_4_out, clock_5_out, clock_6_out, clock_8_out, clock_9_out, clock_10_out, comparator_1_eq,
       comparator_2_eq, comparator_3_eq, comparator_4_eq, comparator_5_eq, comparator_6_eq, comparator_7_eq,
       comparator_8_eq, comparator_9_eq, d_ff_1_qn, d_ff_2_qn, keyboard_1_avail, MemRead, MemWrite, or_1_out,
       or_2_out, or_3_out, or_4_out, rgb_video_1_p2, rgb_video_1_p3, RST, rv_32_im_1_p9, Sync,
       videoram_for_monochrome_display_1_p7;
  wire [6:0] keyboard_1_data;
  wire [31:0] Address, bit_extender_1_out, bit_extender_2_out, Data_in, Data_out, ram_1_dout, ram_2_dout,
       register_1_q, rom_1_data, videoram_for_monochrome_display_1_p8, videoram_for_monochrome_display_1_p9,
       videoram_for_monochrome_display_1_p10, videoram_for_monochrome_display_1_p11,
       videoram_for_monochrome_display_1_p12, videoram_for_monochrome_display_1_p13,
       videoram_for_monochrome_display_1_p14, videoram_for_monochrome_display_1_p15,
       videoram_for_monochrome_display_1_p16, videoram_for_monochrome_display_1_p17,
       videoram_for_monochrome_display_1_p18, videoram_for_monochrome_display_1_p19,
       videoram_for_monochrome_display_1_p20, videoram_for_monochrome_display_1_p21,
       videoram_for_monochrome_display_1_p22, videoram_for_monochrome_display_1_p23,
       videoram_for_monochrome_display_1_p24, videoram_for_monochrome_display_1_p25,
       videoram_for_monochrome_display_1_p26, videoram_for_monochrome_display_1_p27,
       videoram_for_monochrome_display_1_p28, videoram_for_monochrome_display_1_p29,
       videoram_for_monochrome_display_1_p30, videoram_for_monochrome_display_1_p31,
       videoram_for_monochrome_display_1_p32, videoram_for_monochrome_display_1_p33,
       videoram_for_monochrome_display_1_p34, videoram_for_monochrome_display_1_p35,
       videoram_for_monochrome_display_1_p36, videoram_for_monochrome_display_1_p37,
       videoram_for_monochrome_display_1_p38, videoram_for_monochrome_display_1_p39;

  Clock clock_1 (.out(clock_1_out));
  Clock clock_2 (.out(clock_2_out));
  Button button_1 (.out(RST));
  D_Flip_Flop d_ff_1 (.clk(clock_1_out), .D(1'b1), .Qn(d_ff_1_qn));  // open: Q, preset, reset
  or or_1 (or_1_out, d_ff_1_qn, RST);
  and and_1 (and_1_out, Sync, clock_2_out);
  // RGB_Video #(.cursor("No Cursor"), .height(32), .scale(8), .width(32)) rgb_video_1: pin names not known; wires that end beside it: or_1_out, rgb_video_1_p2, rgb_video_1_p3, Address[11:7], Address[6:2], Data_out[23:0]
  Clock clock_3 (.out(rgb_video_1_p2));
  and and_2 (rgb_video_1_p3, MemWrite, comparator_1_eq);
  Comparator #(.width(20)) comparator_1 (.a(20'hffff4), .b(Address[31:12]), .eq(comparator_1_eq));  // open: gt, lt
  // rv_32_im #(.resetAddress('h400000)) rv_32_im_1: pin names not known; wires that end beside it: and_1_out, RST, Data_in, Address, Data_out, MemRead, MemWrite, Sync, rv_32_im_1_p9
  and and_3 (and_3_out, comparator_1_eq, or_2_out);
  or or_2 (or_2_out, MemRead, MemWrite);
  Clock clock_4 (.out(clock_4_out));
  Button button_2 (.out(rv_32_im_1_p9));
  RAM #(.addrWidth(10), .asyncread("true"), .dataWidth(32)) ram_1 (
    .addr(Address[11:2]), .we(rgb_video_1_p3), .oe(1'b1), .clk(clock_4_out), .din(Data_out), .dout(ram_1_dout));
  Comparator #(.width(24)) comparator_2 (.a(Address[31:8]), .b(24'hffff80), .eq(comparator_2_eq));  // open: gt, lt
  Clock clock_5 (.out(clock_5_out));
  Comparator #(.width(16)) comparator_3 (.a(Address[31:16]), .b(16'h40), .eq(comparator_3_eq));  // open: gt, lt
  Comparator #(.width(16)) comparator_4 (.a(Address[31:16]), .b(16'h1001), .eq(comparator_4_eq));  // open: gt, lt
  Comparator #(.width(32)) comparator_5 (.a(Address), .b(32'hffff0010), .eq(comparator_5_eq));  // open: gt, lt
  and and_4 (and_4_out, comparator_2_eq, MemWrite);
  and and_5 (and_5_out, comparator_2_eq, MemRead);
  D_Flip_Flop d_ff_2 (.clk(clock_5_out), .D(1'b1), .Qn(d_ff_2_qn));  // open: Q, preset, reset
  or or_3 (or_3_out, d_ff_2_qn, RST);
  ROM #(.addrWidth(14), .dataWidth(32)) rom_1 (.addr(Address[15:2]), .data(rom_1_data));
  and and_6 (and_6_out, comparator_3_eq, MemRead);
  RAM #(.addrWidth(14), .asyncread("true"), .dataWidth(32)) ram_2 (
    .addr(Address[15:2]), .we(and_7_out), .oe(1'b1), .clk(clock_6_out), .din(Data_out), .dout(ram_2_dout));
  and and_7 (and_7_out, comparator_4_eq, MemWrite);
  Clock clock_6 (.out(clock_6_out));
  or or_4 (or_4_out, MemWrite, MemRead);
  // Videoram_for_monochrome_display videoram_for_monochrome_display_1: pin names not known; wires that end beside it: and_4_out, Address[6:2], Data_out, and_5_out, Data_in, or_3_out, videoram_for_monochrome_display_1_p7, videoram_for_monochrome_display_1_p8, videoram_for_monochrome_display_1_p9, videoram_for_monochrome_display_1_p10, videoram_for_monochrome_display_1_p11, videoram_for_monochrome_display_1_p12, videoram_for_monochrome_display_1_p13, videoram_for_monochrome_display_1_p14, videoram_for_monochrome_display_1_p15, videoram_for_monochrome_display_1_p16, videoram_for_monochrome_display_1_p17, videoram_for_monochrome_display_1_p18, videoram_for_monochrome_display_1_p19, videoram_for_monochrome_display_1_p20, videoram_for_monochrome_display_1_p21, videoram_for_monochrome_display_1_p22, videoram_for_monochrome_display_1_p23, videoram_for_monochrome_display_1_p24, videoram_for_monochrome_display_1_p25, videoram_for_monochrome_display_1_p26, videoram_for_monochrome_display_1_p27, videoram_for_monochrome_display_1_p28, videoram_for_monochrome_display_1_p29, videoram_for_monochrome_display_1_p30, videoram_for_monochrome_display_1_p31, videoram_for_monochrome_display_1_p32, videoram_for_monochrome_display_1_p33, videoram_for_monochrome_display_1_p34, videoram_for_monochrome_display_1_p35, videoram_for_monochrome_display_1_p36, videoram_for_monochrome_display_1_p37, videoram_for_monochrome_display_1_p38, videoram_for_monochrome_display_1_p39
  DotMatrix #(.inputtype("row"), .matrixcols(32), .matrixrows(32)) dotmatrix_1 (
    .row0(videoram_for_monochrome_display_1_p8), .row1(videoram_for_monochrome_display_1_p9),
    .row2(videoram_for_monochrome_display_1_p10), .row3(videoram_for_monochrome_display_1_p11),
    .row4(videoram_for_monochrome_display_1_p12), .row5(videoram_for_monochrome_display_1_p13),
    .row6(videoram_for_monochrome_display_1_p14), .row7(videoram_for_monochrome_display_1_p15),
    .row8(videoram_for_monochrome_display_1_p16), .row9(videoram_for_monochrome_display_1_p17),
    .row10(videoram_for_monochrome_display_1_p18), .row11(videoram_for_monochrome_display_1_p19),
    .row12(videoram_for_monochrome_display_1_p20), .row13(videoram_for_monochrome_display_1_p21),
    .row14(videoram_for_monochrome_display_1_p22), .row15(videoram_for_monochrome_display_1_p23),
    .row16(videoram_for_monochrome_display_1_p24), .row17(videoram_for_monochrome_display_1_p25),
    .row18(videoram_for_monochrome_display_1_p26), .row19(videoram_for_monochrome_display_1_p27),
    .row20(videoram_for_monochrome_display_1_p28), .row21(videoram_for_monochrome_display_1_p29),
    .row22(videoram_for_monochrome_display_1_p30), .row23(videoram_for_monochrome_display_1_p31),
    .row24(videoram_for_monochrome_display_1_p32), .row25(videoram_for_monochrome_display_1_p33),
    .row26(videoram_for_monochrome_display_1_p34), .row27(videoram_for_monochrome_display_1_p35),
    .row28(videoram_for_monochrome_display_1_p36), .row29(videoram_for_monochrome_display_1_p37),
    .row30(videoram_for_monochrome_display_1_p38), .row31(videoram_for_monochrome_display_1_p39));
  Clock clock_7 (.out(videoram_for_monochrome_display_1_p7));
  assign Data_in = and_3_out ? ram_1_dout : 32'bz;  // Controlled_Buffer controlled_buffer_1
  and and_8 (and_8_out, comparator_4_eq, or_4_out);
  Register #(.width(32)) register_1 (.D(Data_out), .en(and_9_out), .Q(register_1_q), .clk(clock_8_out));  // open: clr
  and and_9 (and_9_out, comparator_5_eq, MemWrite);
  Clock clock_8 (.out(clock_8_out));
  and and_10 (and_10_out, comparator_5_eq, MemRead);
  _7_Segment_Display u_7_segment_display_1 (
    .g(register_1_q[14]), .f(register_1_q[13]), .a(register_1_q[8]), .b(register_1_q[9]),
    .e(register_1_q[12]), .d(register_1_q[11]), .c(register_1_q[10]), .dp(register_1_q[15]));
  assign Data_in = and_10_out ? register_1_q : 32'bz;  // Controlled_Buffer controlled_buffer_2
  _7_Segment_Display u_7_segment_display_2 (
    .g(register_1_q[6]), .f(register_1_q[5]), .a(register_1_q[0]), .b(register_1_q[1]), .e(register_1_q[4]),
    .d(register_1_q[3]), .c(register_1_q[2]), .dp(register_1_q[7]));
  assign Data_in = and_6_out ? rom_1_data : 32'bz;  // Controlled_Buffer controlled_buffer_3
  assign Data_in = and_8_out ? ram_2_dout : 32'bz;  // Controlled_Buffer controlled_buffer_4
  Clock clock_9 (.out(clock_9_out));
  TTY tty_1 (.data(Data_out[6:0]), .clk(clock_9_out), .we(and_11_out), .clr(button_3_out));
  and and_11 (and_11_out, comparator_6_eq, MemWrite);
  Button button_3 (.out(button_3_out));
  Comparator #(.width(32)) comparator_6 (.a(Address), .b(32'hffff000c), .eq(comparator_6_eq));  // open: gt, lt
  Clock clock_10 (.out(clock_10_out));
  Comparator #(.width(32)) comparator_7 (.a(Address), .b(32'hffff0004), .eq(comparator_7_eq));  // open: gt, lt
  Keyboard keyboard_1 (
    .clk(clock_10_out), .re(and_12_out), .clr(button_4_out), .avail(keyboard_1_avail), .data(keyboard_1_data));
  Button button_4 (.out(button_4_out));
  and and_12 (and_12_out, comparator_7_eq, MemRead);
  assign bit_extender_1_out = {{25{keyboard_1_data[6]}}, keyboard_1_data};  // Bit_Extender bit_extender_1
  assign bit_extender_2_out = {{31{keyboard_1_avail}}, keyboard_1_avail};  // Bit_Extender bit_extender_2
  Comparator #(.width(32)) comparator_8 (.a(Address), .b(32'hffff0000), .eq(comparator_8_eq));  // open: gt, lt
  and and_13 (and_13_out, comparator_9_eq, MemRead);
  Comparator #(.width(32)) comparator_9 (.a(Address), .b(32'hffff0008), .eq(comparator_9_eq));  // open: gt, lt
  assign Data_in = and_12_out ? bit_extender_1_out : 32'bz;  // Controlled_Buffer controlled_buffer_5
  assign Data_in = and_14_out ? bit_extender_2_out : 32'bz;  // Controlled_Buffer controlled_buffer_6
  and and_14 (and_14_out, comparator_8_eq, MemRead);
  assign Data_in = and_13_out ? 32'h1 : 32'bz;  // Controlled_Buffer controlled_buffer_7

  // Notes on the sheet:
  //   Data in  -->
  //   Reset button
  //   Bitmap Display (Colour)
  //   press to continue
  //   when halted
  //   Address -->
  //   Data out  -->
  //   contents of rom_1 (hex, n*v repeats v):
  //   fc20117 ffc10113 513 593 613 8000ef 6f ff010113 112623 812423 912223 517 1f850513 60000ef 413 497
  //   20048493 741513 a48533 1b4000ef 140413 1f45793 f40433 147413 40f40433 fe1ff06f 41f55793 a7c533
  //   40f50533 8067 ffff07b7 a7a623 8067 ffff07b7 a00713 e7a623 8067 54783 78c63 ffff0737 f72623 150513
  //   54783 fe079ae3 8067 ff010113 41f55813 2d87813 410713 900613 a00593 fff60613 2b567b3 41f7d693 f6c7b3
  //   40d787b3 3078793 f70423 2b54533 fff70713 fc051ee3 80663 ffff07b7 107a623 900793 2c7c263 410793
  //   c787b3 e10693 ffff0637 7c703 e62623 178793 fed79ae3 1010113 8067 ffff07b7 7a503 8067 ffff07b7 47a503
  //   8067 50693 100793 4b7d263 fff58613 513 ffff0737 a00593 72783 fe078ee3 472783 ff7f793 f68023 b78a63
  //   168693 150513 fec510e3 60513 68023 8067 fff00513 8067 100593 513 ffff0737 900613 100813 2d00893
  //   fff00313 200006f fd068793 2f66c63 251793 a787b3 179793 fd068693 f68533 72783 fe078ee3 472683
  //   fc051ce3 fd059ae3 fd1698e3 30593 fe5ff06f 2b50533 8067 ffff82b7 2000313 52383 72a023 428293 450513
  //   fff30313 fe0316e3 8067 70736944 6979616c 7020676e 75746369 2e736572 a2e2e 0 0 0 3ff000 e01c00
  //   3f03f00 7f87f80 ff87fc0 ffcffc0 1ffcffe0 1e7cf9e0 3cb874f0 3e7879f0 3ff03ff0 3fc78ff0 3fcfcff0
  //   3f9fe7f0 3f9fe7f0 1f8fc7e0 1ea015e0 e9025c0 ca794c0 c8844c0 8986440 e01c00 0 303000 3cf000 3ff000
  //   3cf000 303000 6*0 1e00060 61f0050 8008028 10004028 24002014 2a089014 24149014 2008a028 1000a3f0
  //   1000cc08 38077004 38080004 30100006 18600002 78000e2 800192 a43912 13c4f22 124403c 2248000 3c88000
  //   f0000
  //   ROM
  //   RAM
  //   Monochrome Bitmap Display
  //   TDR
  //   RDR
  //   clear
  //   MMIO DIsplay
  //   MMIO Keyboard
  //   clear
  //   clear
  //   RISC-V RV32IM Computer System model by Pavel Gladyshev
  //   licensed under Creative Commons Attribution International license 4.0 
  //   RCR
  //   TCR
  //   Display is always ready
  //   clear
  //   clear
endmodule
