// Logisim project risc_v_rv32im_JAVA.circ as structural Verilog: 1 circuit, main circuit System_JAVA
module System_JAVA (
);

  wire and_1_out, and_3_out, and_4_out, and_5_out, and_6_out, and_7_out, and_8_out, and_9_out, and_10_out,
       and_11_out, and_12_out, and_13_out, and_14_out, button_3_out, button_4_out, clock_1_out, clock_2_out,
       clock_4_out, clock_5_out, clock_6_out, clock_7_out, clock_8_out, comparator_1_eq, comparator_2_eq,
       comparator_3_eq, comparator_4_eq, comparator_5_eq, comparator_6_eq, comparator_7_eq, comparator_8_eq,
       comparator_9_eq, d_ff_1_qn, keyboard_1_avail, MemRead, MemWrite, or_1_out, or_2_out, or_3_out,
       rgb_video_1_p2, rgb_video_1_p3, RST, rv_32_im_1_p9, Sync;
  wire [6:0] keyboard_1_data;
  wire [31:0] Address, bit_extender_1_out, bit_extender_2_out, Data_in, Data_out, ram_1_dout, ram_2_dout,
       register_1_q, rom_1_data, videoram_for_monochrome_display_1_p6, videoram_for_monochrome_display_1_p7,
       videoram_for_monochrome_display_1_p8, videoram_for_monochrome_display_1_p9,
       videoram_for_monochrome_display_1_p10, videoram_for_monochrome_display_1_p11,
       videoram_for_monochrome_display_1_p12, videoram_for_monochrome_display_1_p13,
       videoram_for_monochrome_display_1_p14, videoram_for_monochrome_display_1_p15,
       videoram_for_monochrome_display_1_p16, videoram_for_monochrome_display_1_p17,
       videoram_for_monochrome_display_1_p18, videoram_for_monochrome_display_1_p19,
       videoram_for_monochrome_display_1_p20, videoram_for_monochrome_display_1_p21,
       videoram_for_monochrome_display_1_p22, videoram_for_monochrome_display_1_p23,
       videoram_for_monochrome_display_1_p24, videoram_for_monochrome_display_1_p25,
       videoram_for_monochrome_display_1_p26, videoram_for_monochrome_display_1_p27,
       videoram_for_monochrome_display_1_p28, videoram_for_monochrome_display_1_p29,
       videoram_for_monochrome_display_1_p30, videoram_for_monochrome_display_1_p31,
       videoram_for_monochrome_display_1_p32, videoram_for_monochrome_display_1_p33,
       videoram_for_monochrome_display_1_p34, videoram_for_monochrome_display_1_p35,
       videoram_for_monochrome_display_1_p36, videoram_for_monochrome_display_1_p37;

  Clock clock_1 (.out(clock_1_out));
  Clock clock_2 (.out(clock_2_out));
  Button button_1 (.out(RST));
  D_Flip_Flop d_ff_1 (.clk(clock_1_out), .D(1'b1), .Qn(d_ff_1_qn));  // open: Q, preset, reset
  or or_1 (or_1_out, d_ff_1_qn, RST);
  and and_1 (and_1_out, Sync, clock_2_out);
  // RGB_Video #(.cursor("No Cursor"), .height(32), .scale(8), .width(32)) rgb_video_1: pin names not known; wires that end beside it: or_1_out, rgb_video_1_p2, rgb_video_1_p3, Address[11:7], Address[6:2], Data_out[23:0]
  Clock clock_3 (.out(rgb_video_1_p2));
  and and_2 (rgb_video_1_p3, MemWrite, comparator_1_eq);
  Comparator #(.width(20)) comparator_1 (.a(20'hffff4), .b(Address[31:12]), .eq(comparator_1_eq));  // open: gt, lt
  // rv_32_im #(.resetAddress('h400000)) rv_32_im_1: pin names not known; wires that end beside it: and_1_out, RST, Data_in, Address, Data_out, MemRead, MemWrite, Sync, rv_32_im_1_p9
  and and_3 (and_3_out, comparator_1_eq, or_2_out);
  or or_2 (or_2_out, MemRead, MemWrite);
  Clock clock_4 (.out(clock_4_out));
  Button button_2 (.out(rv_32_im_1_p9));
  RAM #(.addrWidth(10), .asyncread("true"), .dataWidth(32)) ram_1 (
    .addr(Address[11:2]), .we(rgb_video_1_p3), .oe(1'b1), .clk(clock_4_out), .din(Data_out), .dout(ram_1_dout));
  Comparator #(.width(24)) comparator_2 (.a(Address[31:8]), .b(24'hffff80), .eq(comparator_2_eq));  // open: gt, lt
  Comparator #(.width(16)) comparator_3 (.a(Address[31:16]), .b(16'h40), .eq(comparator_3_eq));  // open: gt, lt
  Comparator #(.width(16)) comparator_4 (.a(Address[31:16]), .b(16'h1001), .eq(comparator_4_eq));  // open: gt, lt
  Comparator #(.width(32)) comparator_5 (.a(Address), .b(32'hffff0010), .eq(comparator_5_eq));  // open: gt, lt
  and and_4 (and_4_out, comparator_2_eq, MemWrite);
  and and_5 (and_5_out, comparator_2_eq, MemRead);
  ROM #(.addrWidth(14), .dataWidth(32)) rom_1 (.addr(Address[15:2]), .data(rom_1_data));
  and and_6 (and_6_out, comparator_3_eq, MemRead);
  RAM #(.addrWidth(14), .asyncread("true"), .dataWidth(32)) ram_2 (
    .addr(Address[15:2]), .we(and_7_out), .oe(1'b1), .clk(clock_5_out), .din(Data_out), .dout(ram_2_dout));
  and and_7 (and_7_out, comparator_4_eq, MemWrite);
  Clock clock_5 (.out(clock_5_out));
  or or_3 (or_3_out, MemWrite, MemRead);
  // Videoram_for_monochrome_display videoram_for_monochrome_display_1: pin names not known; wires that end beside it: and_4_out, Address[6:2], Data_out, and_5_out, Data_in, videoram_for_monochrome_display_1_p6, videoram_for_monochrome_display_1_p7, videoram_for_monochrome_display_1_p8, videoram_for_monochrome_display_1_p9, videoram_for_monochrome_display_1_p10, videoram_for_monochrome_display_1_p11, videoram_for_monochrome_display_1_p12, videoram_for_monochrome_display_1_p13, videoram_for_monochrome_display_1_p14, videoram_for_monochrome_display_1_p15, videoram_for_monochrome_display_1_p16, videoram_for_monochrome_display_1_p17, videoram_for_monochrome_display_1_p18, videoram_for_monochrome_display_1_p19, videoram_for_monochrome_display_1_p20, videoram_for_monochrome_display_1_p21, videoram_for_monochrome_display_1_p22, videoram_for_monochrome_display_1_p23, videoram_for_monochrome_display_1_p24, videoram_for_monochrome_display_1_p25, videoram_for_monochrome_display_1_p26, videoram_for_monochrome_display_1_p27, videoram_for_monochrome_display_1_p28, videoram_for_monochrome_display_1_p29, videoram_for_monochrome_display_1_p30, videoram_for_monochrome_display_1_p31, videoram_for_monochrome_display_1_p32, videoram_for_monochrome_display_1_p33, videoram_for_monochrome_display_1_p34, videoram_for_monochrome_display_1_p35, videoram_for_monochrome_display_1_p36, videoram_for_monochrome_display_1_p37
  DotMatrix #(.inputtype("row"), .matrixcols(32), .matrixrows(32)) dotmatrix_1 (
    .row0(videoram_for_monochrome_display_1_p6), .row1(videoram_for_monochrome_display_1_p7),
    .row2(videoram_for_monochrome_display_1_p8), .row3(videoram_for_monochrome_display_1_p9),
    .row4(videoram_for_monochrome_display_1_p10), .row5(videoram_for_monochrome_display_1_p11),
    .row6(videoram_for_monochrome_display_1_p12), .row7(videoram_for_monochrome_display_1_p13),
    .row8(videoram_for_monochrome_display_1_p14), .row9(videoram_for_monochrome_display_1_p15),
    .row10(videoram_for_monochrome_display_1_p16), .row11(videoram_for_monochrome_display_1_p17),
    .row12(videoram_for_monochrome_display_1_p18), .row13(videoram_for_monochrome_display_1_p19),
    .row14(videoram_for_monochrome_display_1_p20), .row15(videoram_for_monochrome_display_1_p21),
    .row16(videoram_for_monochrome_display_1_p22), .row17(videoram_for_monochrome_display_1_p23),
    .row18(videoram_for_monochrome_display_1_p24), .row19(videoram_for_monochrome_display_1_p25),
    .row20(videoram_for_monochrome_display_1_p26), .row21(videoram_for_monochrome_display_1_p27),
    .row22(videoram_for_monochrome_display_1_p28), .row23(videoram_for_monochrome_display_1_p29),
    .row24(videoram_for_monochrome_display_1_p30), .row25(videoram_for_monochrome_display_1_p31),
    .row26(videoram_for_monochrome_display_1_p32), .row27(videoram_for_monochrome_display_1_p33),
    .row28(videoram_for_monochrome_display_1_p34), .row29(videoram_for_monochrome_display_1_p35),
    .row30(videoram_for_monochrome_display_1_p36), .row31(videoram_for_monochrome_display_1_p37));
  assign Data_in = and_3_out ? ram_1_dout : 32'bz;  // Controlled_Buffer controlled_buffer_1
  and and_8 (and_8_out, comparator_4_eq, or_3_out);
  Register #(.width(32)) register_1 (.D(Data_out), .en(and_9_out), .Q(register_1_q), .clk(clock_6_out));  // open: clr
  and and_9 (and_9_out, comparator_5_eq, MemWrite);
  Clock clock_6 (.out(clock_6_out));
  and and_10 (and_10_out, comparator_5_eq, MemRead);
  _7_Segment_Display u_7_segment_display_1 (
    .g(register_1_q[14]), .f(register_1_q[13]), .a(register_1_q[8]), .b(register_1_q[9]),
    .e(register_1_q[12]), .d(register_1_q[11]), .c(register_1_q[10]), .dp(register_1_q[15]));
  assign Data_in = and_10_out ? register_1_q : 32'bz;  // Controlled_Buffer controlled_buffer_2
  _7_Segment_Display u_7_segment_display_2 (
    .g(register_1_q[6]), .f(register_1_q[5]), .a(register_1_q[0]), .b(register_1_q[1]), .e(register_1_q[4]),
    .d(register_1_q[3]), .c(register_1_q[2]), .dp(register_1_q[7]));
  assign Data_in = and_6_out ? rom_1_data : 32'bz;  // Controlled_Buffer controlled_buffer_3
  assign Data_in = and_8_out ? ram_2_dout : 32'bz;  // Controlled_Buffer controlled_buffer_4
  Clock clock_7 (.out(clock_7_out));
  TTY tty_1 (.data(Data_out[6:0]), .clk(clock_7_out), .we(and_11_out), .clr(button_3_out));
  and and_11 (and_11_out, comparator_6_eq, MemWrite);
  Button button_3 (.out(button_3_out));
  Comparator #(.width(32)) comparator_6 (.a(Address), .b(32'hffff000c), .eq(comparator_6_eq));  // open: gt, lt
  Clock clock_8 (.out(clock_8_out));
  Comparator #(.width(32)) comparator_7 (.a(Address), .b(32'hffff0004), .eq(comparator_7_eq));  // open: gt, lt
  Keyboard keyboard_1 (
    .clk(clock_8_out), .re(and_12_out), .clr(button_4_out), .avail(keyboard_1_avail), .data(keyboard_1_data));
  Button button_4 (.out(button_4_out));
  and and_12 (and_12_out, comparator_7_eq, MemRead);
  assign bit_extender_1_out = {{25{keyboard_1_data[6]}}, keyboard_1_data};  // Bit_Extender bit_extender_1
  assign bit_extender_2_out = {{31{keyboard_1_avail}}, keyboard_1_avail};  // Bit_Extender bit_extender_2
  Comparator #(.width(32)) comparator_8 (.a(Address), .b(32'hffff0000), .eq(comparator_8_eq));  // open: gt, lt
  and and_13 (and_13_out, comparator_9_eq, MemRead);
  Comparator #(.width(32)) comparator_9 (.a(Address), .b(32'hffff0008), .eq(comparator_9_eq));  // open: gt, lt
  assign Data_in = and_12_out ? bit_extender_1_out : 32'bz;  // Controlled_Buffer controlled_buffer_5
  assign Data_in = and_14_out ? bit_extender_2_out : 32'bz;  // Controlled_Buffer controlled_buffer_6
  and and_14 (and_14_out, comparator_8_eq, MemRead);
  assign Data_in = and_13_out ? 32'h1 : 32'bz;  // Controlled_Buffer controlled_buffer_7

  // Notes on the sheet:
  //   Data in  -->
  //   Reset button
  //   Bitmap Display (Colour)
  //   press to continue
  //   when halted
  //   Address -->
  //   Data out  -->
  //   contents of rom_1 (hex, n*v repeats v):
  //   ffff0337 1130313 3f00293 530023 600293 530023 5b00293 530023 4f00293 530023 6600293 530023 6d00293
  //   530023 7d00293 530023 700293 530023 7f00293 530023 6f00293 530023 ffff0337 1030313 3f00293 530023
  //   600293 530023 5b00293 530023 4f00293 530023 6600293 530023 6d00293 530023 7d00293 530023 700293
  //   530023 7f00293 530023 6f00293 530023 a00893 73
  //   ROM
  //   RAM
  //   Monochrome Bitmap Display
  //   TDR
  //   RDR
  //   clear
  //   MMIO DIsplay
  //   MMIO Keyboard
  //   clear
  //   clear
  //   RISC-V RV32IM Computer System model by Pavel Gladyshev
  //   licensed under Creative Commons Attribution International license 4.0 
  //   RCR
  //   TCR
  //   Display is always ready
  //   clear
  //   clear
endmodule
