// Logisim project risc_v_rv32im_plic_example.circ as structural Verilog: 1 circuit, main circuit main
module main (
);

  wire and_1_out, and_3_out, and_4_out, and_5_out, and_6_out, and_7_out, and_8_out, and_9_out, and_10_out,
       and_11_out, and_12_out, and_13_out, and_14_out, and_15_out, and_16_out, button_3_out, button_4_out,
       button_5_out, clock_1_out, clock_2_out, clock_3_out, clock_4_out, clock_5_out, clock_8_out,
       clock_9_out, clock_10_out, clock_12_out, clock_13_out, clock_14_out, clock_15_out, comparator_1_eq,
       comparator_2_eq, comparator_3_eq, comparator_4_eq, comparator_5_eq, comparator_6_eq, comparator_7_eq,
       comparator_8_eq, comparator_9_eq, comparator_10_eq, comparator_11_eq, counter_interrupt_1_p5,
       counter_interrupt_1_p7, counter_interrupt_1_p8, counter_interrupt_1_p12, counter_interrupt_1_p14,
       d_ff_1_qn, d_ff_2_qn, d_ff_3_qn, d_ff_4_qn, MemRead, MemWrite, monochrome_videoram_1_p7, or_1_out,
       or_3_out, or_4_out, or_5_out, or_6_out, rgb_video_1_p2, rgb_video_1_p3, RST, s1, s2, Start_out, Sync;
  wire [4:0] slider_1_out;
  wire [6:0] keyboard_1_data, keyboard_2_data;
  wire [31:0] Address, bit_extender_1_out, bit_extender_2_out, bit_extender_3_out, bit_extender_4_out,
       Data_in, Data_out, monochrome_videoram_1_p8, monochrome_videoram_1_p9, monochrome_videoram_1_p10,
       monochrome_videoram_1_p11, monochrome_videoram_1_p12, monochrome_videoram_1_p13,
       monochrome_videoram_1_p14, monochrome_videoram_1_p15, monochrome_videoram_1_p16,
       monochrome_videoram_1_p17, monochrome_videoram_1_p18, monochrome_videoram_1_p19,
       monochrome_videoram_1_p20, monochrome_videoram_1_p21, monochrome_videoram_1_p22,
       monochrome_videoram_1_p23, monochrome_videoram_1_p24, monochrome_videoram_1_p25,
       monochrome_videoram_1_p26, monochrome_videoram_1_p27, monochrome_videoram_1_p28,
       monochrome_videoram_1_p29, monochrome_videoram_1_p30, monochrome_videoram_1_p31,
       monochrome_videoram_1_p32, monochrome_videoram_1_p33, monochrome_videoram_1_p34,
       monochrome_videoram_1_p35, monochrome_videoram_1_p36, monochrome_videoram_1_p37,
       monochrome_videoram_1_p38, monochrome_videoram_1_p39, ram_1_dout, ram_2_dout, register_1_q, rom_1_data;

  Clock clock_1 (.out(clock_1_out));
  or or_1 (or_1_out, d_ff_1_qn, RST);
  Clock clock_2 (.out(clock_2_out));
  D_Flip_Flop d_ff_1 (.clk(clock_2_out), .D(1'b1), .Qn(d_ff_1_qn));  // open: Q, preset, reset
  Clock clock_3 (.out(clock_3_out));
  Clock clock_4 (.out(clock_4_out));
  Button button_1 (.out(RST));
  // counter_interrupt counter_interrupt_1: pin names not known; wires that end beside it: Address, MemWrite, MemRead, Data_out, counter_interrupt_1_p5, Data_in, counter_interrupt_1_p7, counter_interrupt_1_p8, RST, Data_in, counter_interrupt_1_p8, counter_interrupt_1_p12, Sync, counter_interrupt_1_p14
  or or_2 (counter_interrupt_1_p5, d_ff_2_qn, RST);
  D_Flip_Flop d_ff_2 (.clk(clock_1_out), .D(1'b1), .Qn(d_ff_2_qn));  // open: Q, preset, reset
  Clock clock_5 (.out(clock_5_out));
  D_Flip_Flop d_ff_3 (.clk(clock_3_out), .D(1'b1), .Qn(d_ff_3_qn));  // open: Q, preset, reset
  or or_3 (or_3_out, d_ff_3_qn, RST);
  and and_1 (and_1_out, Sync, clock_4_out);
  Clock clock_6 (.out(counter_interrupt_1_p7));
  // plic plic_1: pin names not known; wires that end beside it: Address, MemWrite, MemRead, Data_out, Data_in, or_1_out, clock_5_out, s1, counter_interrupt_1_p12, s2
  // RGB_Video #(.cursor("No Cursor"), .height(32), .scale(8), .width(32)) rgb_video_1: pin names not known; wires that end beside it: or_3_out, rgb_video_1_p2, rgb_video_1_p3, Address[11:7], Address[6:2], Data_out[23:0]
  Clock clock_7 (.out(rgb_video_1_p2));
  and and_2 (rgb_video_1_p3, MemWrite, comparator_1_eq);
  Comparator #(.width(20)) comparator_1 (.a(20'hffff4), .b(Address[31:12]), .eq(comparator_1_eq));  // open: gt, lt
  // rv_32_im #(.hexRegisters("true"), .resetAddress('h400000)) rv_32_im_1: pin names not known; wires that end beside it: and_1_out, Address, Data_out, MemRead, MemWrite
  and and_3 (and_3_out, comparator_1_eq, or_4_out);
  or or_4 (or_4_out, MemRead, MemWrite);
  Clock clock_8 (.out(clock_8_out));
  Button button_2 (.out(counter_interrupt_1_p14));
  RAM #(.addrWidth(10), .asyncread("true"), .dataWidth(32)) ram_1 (
    .addr(Address[11:2]), .we(rgb_video_1_p3), .oe(1'b1), .clk(clock_8_out), .din(Data_out), .dout(ram_1_dout));
  Comparator #(.width(24)) comparator_2 (.a(Address[31:8]), .b(24'hffff80), .eq(comparator_2_eq));  // open: gt, lt
  Clock clock_9 (.out(clock_9_out));
  Comparator #(.width(16)) comparator_3 (.a(Address[31:16]), .b(16'h40), .eq(comparator_3_eq));  // open: gt, lt
  Comparator #(.width(16)) comparator_4 (.a(Address[31:16]), .b(16'h1001), .eq(comparator_4_eq));  // open: gt, lt
  Comparator #(.width(32)) comparator_5 (.a(Address), .b(32'hffff0010), .eq(comparator_5_eq));  // open: gt, lt
  and and_4 (and_4_out, comparator_2_eq, MemWrite);
  and and_5 (and_5_out, comparator_2_eq, MemRead);
  D_Flip_Flop d_ff_4 (.clk(clock_9_out), .D(1'b1), .Qn(d_ff_4_qn));  // open: Q, preset, reset
  or or_5 (or_5_out, d_ff_4_qn, RST);
  ROM #(.addrWidth(14), .dataWidth(32)) rom_1 (.addr(Address[15:2]), .data(rom_1_data));
  and and_6 (and_6_out, comparator_3_eq, MemRead);
  RAM #(.addrWidth(14), .asyncread("true"), .dataWidth(32)) ram_2 (
    .addr(Address[15:2]), .we(and_7_out), .oe(1'b1), .clk(clock_10_out), .din(Data_out), .dout(ram_2_dout));
  and and_7 (and_7_out, comparator_4_eq, MemWrite);
  Clock clock_10 (.out(clock_10_out));
  or or_6 (or_6_out, MemWrite, MemRead);
  // monochrome_videoram monochrome_videoram_1: pin names not known; wires that end beside it: and_4_out, Address[6:2], Data_out, and_5_out, Data_in, or_5_out, monochrome_videoram_1_p7, monochrome_videoram_1_p8, monochrome_videoram_1_p9, monochrome_videoram_1_p10, monochrome_videoram_1_p11, monochrome_videoram_1_p12, monochrome_videoram_1_p13, monochrome_videoram_1_p14, monochrome_videoram_1_p15, monochrome_videoram_1_p16, monochrome_videoram_1_p17, monochrome_videoram_1_p18, monochrome_videoram_1_p19, monochrome_videoram_1_p20, monochrome_videoram_1_p21, monochrome_videoram_1_p22, monochrome_videoram_1_p23, monochrome_videoram_1_p24, monochrome_videoram_1_p25, monochrome_videoram_1_p26, monochrome_videoram_1_p27, monochrome_videoram_1_p28, monochrome_videoram_1_p29, monochrome_videoram_1_p30, monochrome_videoram_1_p31, monochrome_videoram_1_p32, monochrome_videoram_1_p33, monochrome_videoram_1_p34, monochrome_videoram_1_p35, monochrome_videoram_1_p36, monochrome_videoram_1_p37, monochrome_videoram_1_p38, monochrome_videoram_1_p39
  DotMatrix #(.inputtype("row"), .matrixcols(32), .matrixrows(32)) dotmatrix_1 (
    .row0(monochrome_videoram_1_p8), .row1(monochrome_videoram_1_p9), .row2(monochrome_videoram_1_p10),
    .row3(monochrome_videoram_1_p11), .row4(monochrome_videoram_1_p12), .row5(monochrome_videoram_1_p13),
    .row6(monochrome_videoram_1_p14), .row7(monochrome_videoram_1_p15), .row8(monochrome_videoram_1_p16),
    .row9(monochrome_videoram_1_p17), .row10(monochrome_videoram_1_p18), .row11(monochrome_videoram_1_p19),
    .row12(monochrome_videoram_1_p20), .row13(monochrome_videoram_1_p21), .row14(monochrome_videoram_1_p22),
    .row15(monochrome_videoram_1_p23), .row16(monochrome_videoram_1_p24), .row17(monochrome_videoram_1_p25),
    .row18(monochrome_videoram_1_p26), .row19(monochrome_videoram_1_p27), .row20(monochrome_videoram_1_p28),
    .row21(monochrome_videoram_1_p29), .row22(monochrome_videoram_1_p30), .row23(monochrome_videoram_1_p31),
    .row24(monochrome_videoram_1_p32), .row25(monochrome_videoram_1_p33), .row26(monochrome_videoram_1_p34),
    .row27(monochrome_videoram_1_p35), .row28(monochrome_videoram_1_p36), .row29(monochrome_videoram_1_p37),
    .row30(monochrome_videoram_1_p38), .row31(monochrome_videoram_1_p39));
  Clock clock_11 (.out(monochrome_videoram_1_p7));
  assign Data_in = and_3_out ? ram_1_dout : 32'bz;  // Controlled_Buffer controlled_buffer_1
  and and_8 (and_8_out, comparator_4_eq, or_6_out);
  Register #(.width(32)) register_1 (.D(Data_out), .en(and_9_out), .Q(register_1_q), .clk(clock_12_out));  // open: clr
  and and_9 (and_9_out, comparator_5_eq, MemWrite);
  Clock clock_12 (.out(clock_12_out));
  and and_10 (and_10_out, comparator_5_eq, MemRead);
  _7_Segment_Display u_7_segment_display_1 (
    .g(register_1_q[14]), .f(register_1_q[13]), .a(register_1_q[8]), .b(register_1_q[9]),
    .e(register_1_q[12]), .d(register_1_q[11]), .c(register_1_q[10]), .dp(register_1_q[15]));
  assign Data_in = and_10_out ? register_1_q : 32'bz;  // Controlled_Buffer controlled_buffer_2
  _7_Segment_Display u_7_segment_display_2 (
    .g(register_1_q[6]), .f(register_1_q[5]), .a(register_1_q[0]), .b(register_1_q[1]), .e(register_1_q[4]),
    .d(register_1_q[3]), .c(register_1_q[2]), .dp(register_1_q[7]));
  Slider #(.Direction("right_to_left"), .width(5)) slider_1 (.out(slider_1_out));
  assign Data_in = and_6_out ? rom_1_data : 32'bz;  // Controlled_Buffer controlled_buffer_3
  assign Data_in = and_8_out ? ram_2_dout : 32'bz;  // Controlled_Buffer controlled_buffer_4
  Button Start (.out(Start_out));
  assign bit_extender_1_out = {{31{Start_out}}, Start_out};  // Bit_Extender bit_extender_1
  Clock clock_13 (.out(clock_13_out));
  TTY tty_1 (.data(Data_out[6:0]), .clk(clock_13_out), .we(and_11_out), .clr(button_3_out));
  and and_11 (and_11_out, comparator_6_eq, MemWrite);
  Button button_3 (.out(button_3_out));
  Comparator #(.width(32)) comparator_6 (.a(Address), .b(32'hffff000c), .eq(comparator_6_eq));  // open: gt, lt
  Clock clock_14 (.out(clock_14_out));
  Comparator #(.width(32)) comparator_7 (.a(Address), .b(32'hffff0004), .eq(comparator_7_eq));  // open: gt, lt
  Clock clock_15 (.out(clock_15_out));
  Comparator #(.width(32)) comparator_8 (.a(Address), .b(32'hffff0104), .eq(comparator_8_eq));  // open: gt, lt
  Comparator #(.width(32)) comparator_9 (.a(Address), .b(32'hffff01e0), .eq(comparator_9_eq));  // open: gt, lt
  assign bit_extender_2_out = {{27{slider_1_out[4]}}, slider_1_out};  // Bit_Extender bit_extender_2
  Keyboard keyboard_1 (.clk(clock_14_out), .re(and_12_out), .clr(button_4_out), .avail(s1), .data(keyboard_1_data));
  Button button_4 (.out(button_4_out));
  and and_12 (and_12_out, comparator_7_eq, MemRead);
  Keyboard keyboard_2 (.clk(clock_15_out), .re(and_13_out), .clr(button_5_out), .avail(s2), .data(keyboard_2_data));
  Button button_5 (.out(button_5_out));
  and and_13 (and_13_out, comparator_8_eq, MemRead);
  assign Data_in = and_14_out ? bit_extender_1_out : 32'bz;  // Controlled_Buffer controlled_buffer_5
  and and_14 (and_14_out, comparator_9_eq, MemRead);
  assign Data_in = and_15_out ? bit_extender_2_out : 32'bz;  // Controlled_Buffer controlled_buffer_6
  and and_15 (and_15_out, comparator_10_eq, MemRead);
  Comparator #(.width(32)) comparator_10 (.a(Address), .b(32'hffff01e4), .eq(comparator_10_eq));  // open: gt, lt
  assign bit_extender_3_out = {{25{keyboard_1_data[6]}}, keyboard_1_data};  // Bit_Extender bit_extender_3
  assign bit_extender_4_out = {{25{keyboard_2_data[6]}}, keyboard_2_data};  // Bit_Extender bit_extender_4
  and and_16 (and_16_out, comparator_11_eq, MemRead);
  Comparator #(.width(32)) comparator_11 (.a(Address), .b(32'hffff0008), .eq(comparator_11_eq));  // open: gt, lt
  assign Data_in = and_12_out ? bit_extender_3_out : 32'bz;  // Controlled_Buffer controlled_buffer_7
  assign Data_in = and_13_out ? bit_extender_4_out : 32'bz;  // Controlled_Buffer controlled_buffer_8
  assign Data_in = and_16_out ? 32'h1 : 32'bz;  // Controlled_Buffer controlled_buffer_9

  // Notes on the sheet:
  //   Data in  -->
  //   Reset button
  //   Bitmap Display (Colour)
  //   press to continue
  //   when halted
  //   Address -->
  //   Data out  -->
  //   contents of rom_1 (hex, n*v repeats v):
  //   417 bc40413 30541073 8000493 30449073 30046073 20044b7 48493 4a403 3c40413 84a023 40006f ffff04b7
  //   1048493 3f00413 848023 600413 848023 5b00413 848023 4f00413 848023 fe1ff06f ffff04b7 1148493 3f00413
  //   848023 600413 848023 5b00413 848023 4f00413 848023 fe1ff06f fc10417 fc440413 ffff44b7 48493 ffff6937
  //   90913 42983 134a023 440413 448493 ffc90913 ff2496e3 fd1ff06f 34041073 fc10417 f4040413 42403 942423
  //   1242623 1342823 340024f3 942223 341024f3 942023 20049b7 98993 9a903 3c90913 129a023 1442483 fc10417
  //   f0040413 942023 900433 42483 34149073 442483 34049073 842483 c42903 1042983 34002473 30200073
  //   Paddle Control <->
  //   ROM
  //   RAM
  //   Monochrome Bitmap Display
  //   TDR
  //   RDR
  //   RDR
  //   clear
  //   MMIO DIsplay
  //   MMIO Keyboard #1
  //   clear
  //   MMIO Keyboard #2
  //   clear
  //   clear
  //   RISC-V RV32IM Computer System model by Pavel Gladyshev
  //   licensed under Creative Commons Attribution International license 4.0 
  //   clear
  //   TCR
  //   Display is always ready
  //   clear
endmodule
