// Logisim project sample.circ as structural Verilog: 1 circuit, main circuit main
module main (
);

  wire clock_1_out;
  wire [3:0] cpu_1_p2_2, cpu_1_p2_3;
  wire [31:0] cpu_1_p2;

  Clock clock_1 (.out(clock_1_out));
  Hex_Digit_Display hex_digit_display_1 (.value(cpu_1_p2[31:28]));  // open: dp
  Hex_Digit_Display hex_digit_display_2 (.value(cpu_1_p2_3));  // open: dp
  Hex_Digit_Display hex_digit_display_3 (.value(cpu_1_p2[27:24]));  // open: dp
  // cpu cpu_1: pin names not known; wires that end beside it: clock_1_out, {cpu_1_p2[31:24], cpu_1_p2_3, cpu_1_p2_2, cpu_1_p2[15:0]}
  Hex_Digit_Display hex_digit_display_4 (.value(cpu_1_p2_2));  // open: dp
  Hex_Digit_Display hex_digit_display_5 (.value(cpu_1_p2[15:12]));  // open: dp
  Hex_Digit_Display hex_digit_display_6 (.value(cpu_1_p2[11:8]));  // open: dp
  Hex_Digit_Display hex_digit_display_7 (.value(cpu_1_p2[7:4]));  // open: dp
  Hex_Digit_Display hex_digit_display_8 (.value(cpu_1_p2[3:0]));  // open: dp

  // Notes on the sheet:
  //   PC
endmodule
