// Logisim project test.circ as structural Verilog: 1 circuit, main circuit main
module main (
);

  wire and_1_out, and_2_out, and_3_out, and_4_out, clock_1_out, comparator_1_eq, comparator_2_eq,
       comparator_3_eq, rv32im_cpu_1_p5, rv32im_cpu_1_p6;
  wire [31:0] ram_1_dout, rom_1_data, rv32im_cpu_1_p2, rv32im_cpu_1_p3, rv32im_cpu_1_p4;

  Clock clock_1 (.out(clock_1_out));
  // RV32IM_CPU #(.hexRegisters("true")) rv32im_cpu_1: pin names not known; wires that end beside it: clock_1_out, rv32im_cpu_1_p2, rv32im_cpu_1_p3, rv32im_cpu_1_p4, rv32im_cpu_1_p5, rv32im_cpu_1_p6
  and and_1 (and_1_out, rv32im_cpu_1_p6, comparator_2_eq);
  RAM #(.asyncread("true"), .dataWidth(32)) ram_1 (
    .addr(rv32im_cpu_1_p3[9:2]), .we(and_1_out), .oe(1'b1), .clk(clock_1_out), .din(rv32im_cpu_1_p4),
    .dout(ram_1_dout));
  Comparator #(.width(32)) comparator_1 (.a(rv32im_cpu_1_p3), .b(32'hfff00000), .eq(comparator_1_eq));  // open: gt, lt
  Comparator #(.width(22)) comparator_2 (.a(rv32im_cpu_1_p3[31:10]), .b(22'h40), .eq(comparator_2_eq));  // open: gt, lt
  Comparator #(.width(22)) comparator_3 (
    .a(rv32im_cpu_1_p3[31:10]), .b({22{1'b0}}), .eq(comparator_3_eq));  // open: gt, lt
  assign rv32im_cpu_1_p2 = and_3_out ? rom_1_data : 32'bz;  // Controlled_Buffer controlled_buffer_1
  assign rv32im_cpu_1_p2 = and_2_out ? ram_1_dout : 32'bz;  // Controlled_Buffer controlled_buffer_2
  and and_2 (and_2_out, comparator_2_eq, rv32im_cpu_1_p5);
  and and_3 (and_3_out, rv32im_cpu_1_p5, comparator_3_eq);
  ROM #(.dataWidth(32)) rom_1 (.addr(rv32im_cpu_1_p3[9:2]), .data(rom_1_data));
  and and_4 (and_4_out, rv32im_cpu_1_p6, comparator_1_eq);
  TTY tty_1 (.data(rv32im_cpu_1_p4[6:0]), .clk(clock_1_out), .we(and_4_out));  // open: clr

  // Notes on the sheet:
  //   contents of rom_1 (hex, n*v repeats v):
  //   10117 3fc10113 513 593 613 140000ef 6f fd010113 2812623 3010413 fca42e23 fff007b7 fef42423 fe042623
  //   2c0006f fec42783 fdc42703 f707b3 7c783 78713 fe842783 e7a023 fec42783 178793 fef42623 fec42783
  //   fdc42703 f707b3 7c783 fc0794e3 13 13 2c12403 3010113 8067 fa010113 4812e23 6010413 faa42623 fff007b7
  //   fef42223 fac42783 79a63 fe442783 3000713 e7a023 900006f fe042623 3c0006f fec42783 178713 fee42623
  //   fac42683 a00713 2e6e733 279793 ff040693 f687b3 fce7a623 fac42703 a00793 2f747b3 faf42623 fac42783
  //   fcf042e3 fec42783 fff78793 fef42423 300006f fe842783 279793 ff040713 f707b3 fcc7a783 3078713
  //   fe442783 e7a023 fe842783 fff78793 fef42423 fe842783 fc07d8e3 5c12403 6010113 8067 fe010113 112e23
  //   812c23 2010413 fe042623 300006f fec42783 178713 107b7 78693 fec42783 279793 f687b3 e7a023 fec42783
  //   178793 fef42623 fec42703 900793 fce7d6e3 fe042423 fe042223 340006f 107b7 78713 fe442783 279793
  //   f707b3 7a783 fe842703 f707b3 fef42423 fe442783 178793 fef42223 fe442703 900793 fce7d4e3 22c00513
  //   e2dff0ef a00513 e95ff0ef 24800513 e1dff0ef fe842503 e85ff0ef 25000513 e0dff0ef 793 78513 1c12083
  //   1812403 2010113 8067 206d7553 6e20666f 65626d75 66207372 206d6f72 6f742031 20 3a736920 20 a
endmodule
