// Logisim project test.circ as structural Verilog: 1 circuit, main circuit main
module main (
);

  wire button_1_out, clock_1_out;
  wire [31:0] CPU1_p3, CPU1_p4;

  Button button_1 (.out(button_1_out));
  Clock clock_1 (.out(clock_1_out));
  // RV32IM_CPU #(.resetAddress('h400000)) CPU1: pin names not known; wires that end beside it: clock_1_out, button_1_out, CPU1_p3, CPU1_p4
  ROM #(.dataWidth(32)) rom_1 (.addr(CPU1_p4[9:2]), .data(CPU1_p3));

  // Notes on the sheet:
  //   contents of rom_1 (hex, n*v repeats v):
  //   300093
endmodule
