// Logisim project test.circ as structural Verilog: 1 circuit, main circuit main
module main (
);

  wire and_1_out, and_2_out, and_3_out, and_4_out, and_5_out, and_6_out, and_7_out, and_8_out, and_9_out,
       and_10_out, and_11_out, and_12_out, and_13_out, clock_1_out, clock_2_out, clock_3_out, clock_4_out,
       clock_5_out, clock_6_out, clock_7_out, clock_8_out, comparator_1_eq, comparator_2_eq, comparator_3_eq,
       comparator_4_gt, comparator_5_lt, comparator_6_eq, comparator_7_eq, comparator_8_eq, comparator_9_eq,
       comparator_10_eq, comparator_11_eq, keyboard_1_avail, keyboard_2_avail, rv32im_cpu_1_p2,
       rv32im_cpu_1_p5, rv32im_cpu_1_p6, rv32im_cpu_1_p7, rv32im_cpu_1_p8, rv32im_cpu_1_p9, rv32im_cpu_1_p10,
       rv32im_cpu_1_p11;
  wire [6:0] keyboard_1_data, keyboard_2_data;
  wire [31:0] bit_extender_1_out, bit_extender_2_out, bit_extender_3_out, bit_extender_4_out, rom_1_data,
       rv32im_cpu_1_p3, rv32im_cpu_1_p4;

  Clock clock_1 (.out(clock_1_out));
  // RV32IM_CPU #(.hexRegisters("true")) rv32im_cpu_1: pin names not known; wires that end beside it: clock_1_out, rv32im_cpu_1_p2, rv32im_cpu_1_p3, rv32im_cpu_1_p4, rv32im_cpu_1_p5, rv32im_cpu_1_p6, rv32im_cpu_1_p7, rv32im_cpu_1_p8, rv32im_cpu_1_p9, rv32im_cpu_1_p10, rv32im_cpu_1_p11
  Pull_Resistor pull_resistor_1 (.node(rv32im_cpu_1_p5));
  Pull_Resistor pull_resistor_2 (.node(rv32im_cpu_1_p6));
  Pull_Resistor pull_resistor_3 ();  // open: node
  and and_1 (and_1_out, rv32im_cpu_1_p6, and_4_out);
  and and_2 (and_2_out, and_4_out, rv32im_cpu_1_p5);
  RAM #(.addrWidth(14), .asyncread("true"), .byteenables("byteEnables"), .dataWidth(32), .databus("bidir")) ram_1 (
    .addr(rv32im_cpu_1_p3[15:2]), .we(and_1_out), .oe(and_2_out), .clk(clock_2_out), .data(rv32im_cpu_1_p4),
    .be3(rv32im_cpu_1_p11), .be2(rv32im_cpu_1_p10), .be1(rv32im_cpu_1_p9), .be0(rv32im_cpu_1_p8));
  Clock clock_2 (.out(clock_2_out));
  Comparator #(.width(32)) comparator_1 (.a(rv32im_cpu_1_p3), .b(32'hfff00000), .eq(comparator_1_eq));  // open: gt, lt
  Comparator #(.width(16)) comparator_2 (
    .a(rv32im_cpu_1_p3[31:16]), .b({16{1'b0}}), .eq(comparator_2_eq));  // open: gt, lt
  Comparator #(.width(16)) comparator_3 (.a(rv32im_cpu_1_p3[31:16]), .b(16'h11), .eq(comparator_3_eq));  // open: gt, lt
  Comparator #(.width(16)) comparator_4 (
    .a(rv32im_cpu_1_p3[31:16]), .b({16{1'b0}}), .gt(comparator_4_gt));  // open: eq, lt
  and and_3 (and_3_out, rv32im_cpu_1_p5, comparator_2_eq);
  Comparator #(.width(16)) comparator_5 (.a(rv32im_cpu_1_p3[31:16]), .b(16'h3), .lt(comparator_5_lt));  // open: gt, eq
  Pull_Resistor pull_resistor_4 (.node(comparator_5_lt));
  and and_4 (and_4_out, comparator_5_lt, comparator_4_gt);
  ROM #(.addrWidth(14), .dataWidth(32)) rom_1 (.addr(rv32im_cpu_1_p3[15:2]), .data(rom_1_data));
  Clock clock_3 (.out(clock_3_out));
  and and_5 (and_5_out, rv32im_cpu_1_p6, comparator_1_eq);
  TTY #(.cols(100), .rows(40)) tty_1 (.data(rv32im_cpu_1_p4[6:0]), .clk(clock_3_out), .we(and_5_out));  // open: clr
  assign rv32im_cpu_1_p4 = and_3_out ? rom_1_data : 32'bz;  // Controlled_Buffer controlled_buffer_1
  and and_6 (and_6_out, rv32im_cpu_1_p5, comparator_3_eq);
  and and_7 (and_7_out, rv32im_cpu_1_p6, comparator_3_eq);
  Clock clock_4 (.out(clock_4_out));
  Comparator #(.width(32)) comparator_6 (.a(rv32im_cpu_1_p3), .b(32'hfff00100), .eq(comparator_6_eq));  // open: gt, lt
  Comparator #(.width(32)) comparator_7 (.a(rv32im_cpu_1_p3), .b(32'hfff00200), .eq(comparator_7_eq));  // open: gt, lt
  Comparator #(.width(32)) comparator_8 (.a(rv32im_cpu_1_p3), .b(32'hfff00104), .eq(comparator_8_eq));  // open: gt, lt
  Comparator #(.width(32)) comparator_9 (.a(rv32im_cpu_1_p3), .b(32'hfff00204), .eq(comparator_9_eq));  // open: gt, lt
  // Hard_Drive_DMA #(.file_name("circuits/testFileSystem/hard_drive.bin")) hard_drive_dma_1: pin names not known; wires that end beside it: rv32im_cpu_1_p3, and_6_out, and_7_out, rv32im_cpu_1_p11, rv32im_cpu_1_p10, rv32im_cpu_1_p9, rv32im_cpu_1_p8, rv32im_cpu_1_p7, clock_4_out, rv32im_cpu_1_p4, rv32im_cpu_1_p5, rv32im_cpu_1_p6, rv32im_cpu_1_p3, rv32im_cpu_1_p2
  Clock clock_5 (.out(clock_5_out));
  Keyboard keyboard_1 (
    .clk(clock_5_out), .re(and_8_out), .avail(keyboard_1_avail), .data(keyboard_1_data));  // open: clr
  and and_8 (and_8_out, comparator_6_eq, rv32im_cpu_1_p5);
  and and_9 (and_9_out, comparator_7_eq, rv32im_cpu_1_p5);
  Clock clock_6 (.out(clock_6_out));
  Keyboard keyboard_2 (
    .clk(clock_6_out), .re(and_10_out), .avail(keyboard_2_avail), .data(keyboard_2_data));  // open: clr
  and and_10 (and_10_out, comparator_8_eq, rv32im_cpu_1_p5);
  and and_11 (and_11_out, comparator_9_eq, rv32im_cpu_1_p5);
  assign bit_extender_1_out = {{25{1'b0}}, keyboard_1_data};  // Bit_Extender bit_extender_1
  assign rv32im_cpu_1_p4 = and_8_out ? bit_extender_1_out : 32'bz;  // Controlled_Buffer controlled_buffer_2
  assign bit_extender_2_out = {{31{1'b0}}, keyboard_1_avail};  // Bit_Extender bit_extender_2
  assign rv32im_cpu_1_p4 = and_9_out ? bit_extender_2_out : 32'bz;  // Controlled_Buffer controlled_buffer_3
  assign bit_extender_3_out = {{25{1'b0}}, keyboard_2_data};  // Bit_Extender bit_extender_3
  assign rv32im_cpu_1_p4 = and_10_out ? bit_extender_3_out : 32'bz;  // Controlled_Buffer controlled_buffer_4
  assign bit_extender_4_out = {{31{1'b0}}, keyboard_2_avail};  // Bit_Extender bit_extender_4
  assign rv32im_cpu_1_p4 = and_11_out ? bit_extender_4_out : 32'bz;  // Controlled_Buffer controlled_buffer_5
  TTY #(.cols(100), .rows(40)) tty_2 (.data(rv32im_cpu_1_p4[6:0]), .clk(clock_7_out), .we(and_12_out));  // open: clr
  Clock clock_7 (.out(clock_7_out));
  Clock clock_8 (.out(clock_8_out));
  TTY tty_3 (.data(rv32im_cpu_1_p4[6:0]), .clk(clock_8_out), .we(and_13_out));  // open: clr
  Comparator #(.width(32)) comparator_10 (
    .a(rv32im_cpu_1_p3), .b(32'hfff00004), .eq(comparator_10_eq));  // open: gt, lt
  and and_12 (and_12_out, comparator_10_eq, rv32im_cpu_1_p6);
  Comparator #(.width(32)) comparator_11 (
    .a(rv32im_cpu_1_p3), .b(32'hfff00008), .eq(comparator_11_eq));  // open: gt, lt
  and and_13 (and_13_out, comparator_11_eq, rv32im_cpu_1_p6);

  // Notes on the sheet:
  //   contents of rom_1 (hex, n*v repeats v):
  //   1b117 ffc10113 513 593 613 454000ef 6f fc010113 2112e23 2812c23 4010413 50793 fcf407a3 77b7 ac78793
  //   7a603 47a683 87a703 fcc42e23 fed42023 fee42223 c7a703 fee42423 107c783 fef40623 fcf44783 47d793
  //   ff7f793 f7f793 ff078793 8787b3 fec7c783 fcf40c23 fcf44783 f7f793 ff078793 8787b3 fec7c783 fcf40ca3
  //   fc040d23 fd840793 78513 6f4000ef 13 3c12083 3812403 4010113 8067 dc010113 22112e23 22812c23 24010413
  //   dca42623 dcb42423 77b7 c078513 6bc000ef 593 dcc42503 174020ef fea42023 107b7 9078693 fe042703 70793
  //   179793 e787b3 279793 f687b3 7a023 fe042623 dc842783 fef42423 77b7 e078513 670000ef dc842783 78513
  //   59c000ef 800006f fdc42703 ddc40793 70613 78593 fe842503 3fd050ef fdc42783 fe842703 f707b3 fef42423
  //   fec42703 fdc42783 f707b3 fef42623 77b7 10078513 61c000ef fdc42503 54c000ef 77b7 10878513 608000ef
  //   fdc42783 40f007b3 fe842703 f707b3 78513 528000ef 77b7 11c78513 5e4000ef ddc40793 20000613 78593
  //   fe042503 2f1020ef fca42e23 fdc42783 f6f044e3 fe042503 314030ef 77b7 12078513 5b0000ef fec42503
  //   4e0000ef 77b7 11c78513 59c000ef 77b7 14c78513 590000ef fe042223 340006f fe442703 dc842783 f707b3
  //   7c783 78513 df1ff0ef 77b7 16478513 564000ef fe442783 178793 fef42223 fe442703 f00793 e7c863 fe442703
  //   fec42783 faf74ee3 77b7 11c78513 534000ef fec42783 78513 23c12083 23812403 24010113 8067 ff010113
  //   112623 812423 1010413 200593 77b7 16878513 7c1010ef 50793 7dc63 613 100593 77b7 16878513 571040ef
  //   200593 77b7 17478513 795010ef 50793 7dc63 100613 100593 77b7 17478513 545040ef 13 c12083 812403
  //   1010113 8067 fe010113 112e23 812c23 2010413 1b5b7 77b7 18078513 da5ff0ef fea42623 fec42783 f04c63
  //   77b7 18878513 468000ef fff00793 1180006f 77b7 1a078513 454000ef fec42503 384000ef 77b7 11c78513
  //   440000ef 9000613 593 107b7 78513 d9050ef 10793 fef42423 107b7 78793 fe842703 e7a223 107b7 78793
  //   1b737 e7a623 107b7 78793 1f737 e7ac23 67b7 3a878713 107b7 78793 e7a423 77b7 1c478513 3d4000ef 107b7
  //   78793 c7a783 78513 2f8000ef 77b7 11c78513 3b4000ef 77b7 1dc78513 3a8000ef 107b7 78793 187a783 78513
  //   2cc000ef 77b7 11c78513 388000ef 77b7 1f478513 37c000ef 107b7 78793 87a783 78513 2a0000ef 77b7
  //   11c78513 35c000ef 107b7 78793 7a023 793 78513 1c12083 1812403 2010113 8067 fe010113 112e23 812c23
  //   2010413 4000513 258000ef 77b7 21078513 1b5060ef 248020ef 50793 7da63 77b7 22478513 19d060ef 880006f
  //   12c000ef 304060ef 50793 7d863 77b7 24878513 17d060ef 77b7 27078513 2d0000ef 200593 77b7 18078513
  //   585010ef fea42623 e1dff0ef 50793 2079863 77b7 29078513 2a4000ef 107b7 78593 77b7 f7c78513 23d060ef
  //   107b7 78513 305060ef 77b7 2bc78513 278000ef 6f 1c12083 1812403 2010113 8067 fe010113 112e23 812c23
  //   2010413 fea42623 feb42423 fec42223 fed42023 fe042683 fe442603 fe842583 fec42503 795050ef 50793 78513
  //   1c12083 1812403 2010113 8067 fe010113 112e23 812c23 2010413 fea42623 feb42423 fec42223 fed42023
  //   fe042683 fe442603 fe842583 fec42503 500060ef 50793 78513 1c12083 1812403 2010113 8067 fe010113
  //   112e23 812c23 2010413 fe042223 fe042423 fe042623 58800793 fef42223 53c00793 fef42423 fe440793 78593
  //   100513 5bd040ef 13 1c12083 1812403 2010113 8067 fe010113 112e23 812c23 2010413 50793 fef407a3
  //   fff007b7 fef44703 e78023 13 1c12083 1812403 2010113 8067 fe010113 112e23 812c23 2010413 fea42623
  //   fec42783 7cc63 107b7 7f078793 7a783 fec42703 f74663 793 300006f fec42503 198010ef 50793 7d663 793
  //   180006f fec42783 679713 117b7 c0878793 f707b3 78513 1c12083 1812403 2010113 8067 fe010113 112e23
  //   812c23 2010413 fea42623 fec42783 79863 3000513 f31ff0ef 940006f fec42783 7dc63 2d00513 f1dff0ef
  //   fec42783 40f007b3 fef42623 fec42703 900793 2e7d463 fec42783 66666737 66770713 2e79733 40275713
  //   41f7d793 40f707b3 78513 f91ff0ef fec42703 666667b7 66778793 2f717b3 4027d693 41f75793 40f686b3 68793
  //   279793 d787b3 179793 40f706b3 ff6f793 3078793 ff7f793 78513 e9dff0ef 1c12083 1812403 2010113 8067
  //   fe010113 112e23 812c23 2010413 fea42623 fec42503 688060ef 13 1c12083 1812403 2010113 8067 ff010113
  //   112623 812423 1010413 77b7 2d078513 fb9ff0ef 77b7 2e478513 fadff0ef 107b7 7f078793 7a783 78513
  //   ed1ff0ef 77b7 2ec78513 f8dff0ef 107b7 7f078793 47a783 78513 eb1ff0ef 77b7 2f878513 f6dff0e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
endmodule
