// Logisim project test.circ as structural Verilog: 1 circuit, main circuit main
module main (
);

  wire and_1_out, and_2_out, and_3_out, and_4_out, and_5_out, and_6_out, clock_1_out, clock_2_out,
       clock_3_out, comparator_1_eq, comparator_2_eq, comparator_3_eq, comparator_4_eq, hard_drive_dma_1_p9,
       hard_drive_dma_1_p10, rv32im_cpu_1_p2, rv32im_cpu_1_p5, rv32im_cpu_1_p6, rv32im_cpu_1_p7,
       rv32im_cpu_1_p8, rv32im_cpu_1_p9, rv32im_cpu_1_p10, rv32im_cpu_1_p11;
  wire [31:0] rom_1_data, rv32im_cpu_1_p3, rv32im_cpu_1_p4;

  Clock clock_1 (.out(clock_1_out));
  // RV32IM_CPU #(.hexRegisters("true")) rv32im_cpu_1: pin names not known; wires that end beside it: clock_1_out, rv32im_cpu_1_p2, rv32im_cpu_1_p3, rv32im_cpu_1_p4, rv32im_cpu_1_p5, rv32im_cpu_1_p6, rv32im_cpu_1_p7, rv32im_cpu_1_p8, rv32im_cpu_1_p9, rv32im_cpu_1_p10, rv32im_cpu_1_p11
  Pull_Resistor pull_resistor_1 (.node(rv32im_cpu_1_p5));
  Pull_Resistor pull_resistor_2 (.node(rv32im_cpu_1_p6));
  and and_1 (and_1_out, comparator_4_eq, rv32im_cpu_1_p5);
  and and_2 (and_2_out, rv32im_cpu_1_p6, comparator_4_eq);
  Clock clock_2 (.out(clock_2_out));
  RAM #(.addrWidth(9), .asyncread("true"), .byteenables("byteEnables"), .dataWidth(32), .databus("bidir")) ram_1 (
    .addr(rv32im_cpu_1_p3[10:2]), .we(and_2_out), .oe(and_1_out), .clk(clock_2_out), .data(rv32im_cpu_1_p4),
    .be3(rv32im_cpu_1_p11), .be2(rv32im_cpu_1_p10), .be1(rv32im_cpu_1_p9), .be0(rv32im_cpu_1_p8));
  Comparator #(.width(32)) comparator_1 (.a(rv32im_cpu_1_p3), .b(32'hfff00000), .eq(comparator_1_eq));  // open: gt, lt
  and and_3 (and_3_out, rv32im_cpu_1_p5, comparator_2_eq);
  Comparator #(.width(20)) comparator_2 (
    .a(rv32im_cpu_1_p3[31:12]), .b({20{1'b0}}), .eq(comparator_2_eq));  // open: gt, lt
  Comparator #(.width(20)) comparator_3 (.a(rv32im_cpu_1_p3[31:12]), .b(20'h11), .eq(comparator_3_eq));  // open: gt, lt
  Comparator #(.width(20)) comparator_4 (.a(rv32im_cpu_1_p3[31:12]), .b(20'h10), .eq(comparator_4_eq));  // open: gt, lt
  ROM #(.dataWidth(32)) rom_1 (.addr(rv32im_cpu_1_p3[9:2]), .data(rom_1_data));
  and and_4 (and_4_out, rv32im_cpu_1_p6, comparator_1_eq);
  Clock clock_3 (.out(clock_3_out));
  TTY tty_1 (.data(rv32im_cpu_1_p4[6:0]), .clk(clock_3_out), .we(and_4_out));  // open: clr
  assign rv32im_cpu_1_p4 = and_3_out ? rom_1_data : 32'bz;  // Controlled_Buffer controlled_buffer_1
  and and_5 (and_5_out, rv32im_cpu_1_p5, comparator_3_eq);
  and and_6 (and_6_out, rv32im_cpu_1_p6, comparator_3_eq);
  // Hard_Drive_DMA hard_drive_dma_1: pin names not known; wires that end beside it: rv32im_cpu_1_p3, and_5_out, and_6_out, rv32im_cpu_1_p11, rv32im_cpu_1_p10, rv32im_cpu_1_p9, rv32im_cpu_1_p8, rv32im_cpu_1_p7, hard_drive_dma_1_p9, hard_drive_dma_1_p10, hard_drive_dma_1_p10, rv32im_cpu_1_p4, rv32im_cpu_1_p5, rv32im_cpu_1_p6, rv32im_cpu_1_p3, rv32im_cpu_1_p2
  Clock clock_4 (.out(hard_drive_dma_1_p9));

  // Notes on the sheet:
  //   contents of rom_1 (hex, n*v repeats v):
  //   10117 7fc10113 513 593 613 40000ef 6f fd010113 2812623 3010413 50793 fcf40fa3 fff007b7 fef42623
  //   fec42783 fdf44703 e78023 13 2c12403 3010113 8067 fe010113 112e23 812c23 2010413 107b7 78793 abcdb737
  //   bcd70713 e7a023 fe042623 2c0006f 107b7 78713 fec42783 279793 f707b3 fec42703 e7a023 fec42783 178793
  //   fef42623 fec42703 7f00793 fce7d8e3 1b802783 10737 70713 e7a023 1bc02783 7a023 1b402783 200713 e7a023
  //   13 1c002783 7a783 17f793 fe079ae3 107b7 deadc737 eef70713 40e7a023 1b802783 10737 20070713 e7a023
  //   1bc02783 7a023 1b402783 100713 e7a023 13 1c002783 7a783 17f793 fe079ae3 100793 fef42423 fe042223
  //   340006f 107b7 20078713 fe442783 279793 f707b3 7a783 fe442703 f70463 fe042423 fe442783 178793
  //   fef42223 fe442703 7f00793 fce7d4e3 fe842783 78863 2b00513 e91ff0ef c0006f 2d00513 e85ff0ef 793 78513
  //   1c12083 1812403 2010113 8067 11000 11004 11008 1100c
endmodule
