// Logisim project test_modified_RAM.circ as structural Verilog: 1 circuit, main circuit main
module main (
);

  wire and_1_out, and_2_out, and_3_out, and_4_out, button_1_out, clock_1_out, clock_2_out, clock_3_out,
       comparator_1_eq, comparator_2_eq, CPU1_p9, d_ff_1_qn, MemRead, MemWrite, or_1_out, or_2_out, Sync;
  wire [31:0] CPU1_p3, CPU1_p4, CPU1_p5, ram_1_dout, rom_1_data;

  Clock clock_1 (.out(clock_1_out));
  D_Flip_Flop d_ff_1 (.clk(clock_1_out), .D(1'b1), .Qn(d_ff_1_qn));  // open: Q, preset, reset
  and and_1 (and_1_out, Sync, clock_2_out);
  Clock clock_2 (.out(clock_2_out));
  Button button_1 (.out(button_1_out));
  or or_1 (or_1_out, button_1_out, d_ff_1_qn);
  // RV32IM_CPU #(.resetAddress('h400000)) CPU1: pin names not known; wires that end beside it: and_1_out, or_1_out, CPU1_p3, CPU1_p4, CPU1_p5, MemRead, MemWrite, Sync, CPU1_p9
  Button button_2 (.out(CPU1_p9));
  Comparator #(.width(16)) comparator_1 (.a(CPU1_p4[31:16]), .b(16'h40), .eq(comparator_1_eq));  // open: gt, lt
  Comparator #(.width(16)) comparator_2 (.a(CPU1_p4[31:16]), .b(16'h1001), .eq(comparator_2_eq));  // open: gt, lt
  ROM #(.addrWidth(14), .dataWidth(32)) rom_1 (.addr(CPU1_p4[15:2]), .data(rom_1_data));
  and and_2 (and_2_out, comparator_1_eq, MemRead);
  RAM #(.addrWidth(14), .asyncread("true"), .dataWidth(32)) ram_1 (
    .addr(CPU1_p4[15:2]), .we(and_3_out), .oe(1'b1), .clk(clock_3_out), .din(CPU1_p5), .dout(ram_1_dout));
  and and_3 (and_3_out, comparator_2_eq, MemWrite);
  Clock clock_3 (.out(clock_3_out));
  or or_2 (or_2_out, MemWrite, MemRead);
  and and_4 (and_4_out, comparator_2_eq, or_2_out);
  assign CPU1_p3 = and_2_out ? rom_1_data : 32'bz;  // Controlled_Buffer controlled_buffer_1
  assign CPU1_p3 = and_4_out ? ram_1_dout : 32'bz;  // Controlled_Buffer controlled_buffer_2

  // Notes on the sheet:
  //   RST
  //   Continue
  //   Address >>
  //   Data Out >>
  //   contents of rom_1 (hex, n*v repeats v):
  //   23056c17 789c0c13 12345bb7 678b8b93 6f
  //   RAM
endmodule
