// Logisim project test_sync.circ as structural Verilog: 1 circuit, main circuit main
module main (
);

  wire and_1_out, button_1_out, clock_1_out, CPU1_p6, Sync;
  wire [31:0] CPU1_p3, CPU1_p4;

  Clock clock_1 (.out(clock_1_out));
  Button button_1 (.out(button_1_out));
  and and_1 (and_1_out, Sync, clock_1_out);
  // RV32IM_CPU #(.resetAddress('h400000)) CPU1: pin names not known; wires that end beside it: and_1_out, button_1_out, CPU1_p3, CPU1_p4, Sync, CPU1_p6
  ROM #(.dataWidth(32)) rom_1 (.addr(CPU1_p4[9:2]), .data(CPU1_p3));
  Button button_2 (.out(CPU1_p6));

  // Notes on the sheet:
  //   contents of rom_1 (hex, n*v repeats v):
  //   300093
endmodule
